# Fritzing sketch Pushbullet (saved by Fritzing 0.9.2b)
breadboards: 1

parts:
  Part1 = Arduino Uno (Rev3)
  OLED1 = 128x32 I2C Monochrome OLED Display
  CC3K1 = Adafruit CC3000 WiFi Breakout
  R1 = Resistor [tolerance=±5% resistance=10k package=THT]
  S1 = Pushbutton [package="[THT]"]
  R2 = Resistor [tolerance=±5% resistance=10k package=THT]
  S2 = Pushbutton [package="[THT]"]

nets:
  N1: Part1.A4/SDA, OLED1.SDA
  N2: Part1.A5/SCL, OLED1.SCL
  N3: Part1.D10_PWM/SS, CC3K1.CS
  N4: Part1.D11_PWM/MOSI, CC3K1.MOSI
  N5: Part1.D12/MISO, CC3K1.MISO
  N6: Part1.D13/SCK, CC3K1.CLK
  GND: Part1.GND, OLED1.GND, CC3K1.GND#1, R1.Pin_1, R2.Pin_1
  N7: Part1.D2, R1.Pin_0, S1.Pin_1, S1.Pin_2
  N8: Part1.D3_PWM, CC3K1.IRQ
  N9: Part1.D4, OLED1.RST
  N10: Part1.D5_PWM, CC3K1.VBEN
  N11: Part1.D6_PWM, R2.Pin_0, S2.Pin_1, S2.Pin_2
  VIN: Part1.5V, OLED1.VIN, CC3K1.VIN, S1.Pin_3, S1.Pin_4, S2.Pin_3, S2.Pin_4
  N12: CC3K1.GND#10, CC3K1.TXD, CC3K1.RXD

custom parts:
  Adafruit CC3000 WiFi Breakout: CC3000 WiFi Breakout
